// Digital circuit T1A3.dig as structural Verilog
module T1A3 (
  input  P,
  input  EN0,
  input  J0,
  input  J1,
  input  J2,
  input  J3,
  output S0
);

  wire and_1_out, nand_1_out, nand_2_out, nand_3_out, nand_4_out, not_1_out, not_2_out, not_3_out, not_4_out,
       or_1_out, or_2_out, or_3_out;

  not not_1 (not_1_out, P);
  or or_1 (or_1_out, J0, J1);
  not not_2 (not_2_out, J2);
  not not_3 (not_3_out, J3);
  or or_2 (or_2_out, or_1_out, not_2_out);
  or or_3 (or_3_out, or_2_out, not_3_out);
  and and_1 (and_1_out, EN0, or_3_out);
  not not_4 (not_4_out, and_1_out);
  nand nand_1 (nand_1_out, not_1_out, nand_2_out);
  nand nand_2 (nand_2_out, nand_1_out, EN0);
  nand nand_3 (nand_3_out, EN0, nand_4_out);
  nand nand_4 (nand_4_out, nand_3_out, not_4_out);
  or or_4 (S0, nand_1_out, nand_4_out);
endmodule
